# Fritzing sketch hardware (saved by Fritzing 0.7.12b)
breadboards: 1

parts:
  Arduino_Uno = Arduino
  10K = Rotary Potentiometer (Small) [maximum_resistance=100kΩ]

nets:
  N1: Arduino_Uno.+5V, 10K.leg2
  N2: Arduino_Uno.GND, 10K.leg1
  N3: Arduino_Uno.A0, 10K.wiper
