# Fritzing sketch hardware (saved by Fritzing 0.7.12b)
breadboards: 1

parts:
  Arduino_Uno = Arduino
  10K = Rotary Potentiometer (Small) [maximum_resistance=100kΩ]
  Button = Pushbutton [package=THT]
  10K_2 = Resistor [tolerance=±5% resistance=220 package=THT]

nets:
  N1: Arduino_Uno.D2, Button.leg1, 10K_2.Pin_0
  N2: Arduino_Uno.+5V, 10K.leg2, Button.leg0
  N3: Arduino_Uno.GND, 10K.leg1, 10K_2.Pin_1
  N4: Arduino_Uno.A0, 10K.wiper
