# Fritzing sketch hardware (saved by Fritzing 0.7.12b)
breadboards: 1

parts:
  Arduino_Uno = Arduino
  10K = Resistor [tolerance=±5% resistance=220 package=THT]
  Button = Pushbutton [package=THT]

nets:
  N1: Arduino_Uno.D2, 10K.Pin_0, Button.leg0
  N2: Arduino_Uno.+5V, Button.leg1
  N3: Arduino_Uno.GND, 10K.Pin_1
